// Logisim project ALU8.circ as structural Verilog: 1 circuit, main circuit main
module main (
  input  [7:0] x,
  input  [7:0] y,
  input  zx,
  input  nx,
  input  zy,
  input  ny,
  input  f,
  input  no
);
endmodule
