// Logisim project And8.circ as structural Verilog: 1 circuit, main circuit And 8 bits
module And_8_bits (
  input  [7:0] in_1,
  input  [7:0] in_2,
  output [7:0] out_3
);

  assign out_3 = in_1 & in_2;  // AND_Gate and_1, 8 bits wide
endmodule
