// Logisim project Sumador.circ as structural Verilog: 1 circuit, main circuit main
module main (
  input  C,
  input  x,
  input  y,
  output out_4,
  output out_5
);

  wire main_1_out_3, main_1_out_4, Semisumador_out_4;

  SemiSUM_main main_1 (.in_1(x), .in_2(y), .out_3(main_1_out_3), .out_4(main_1_out_4));
  SemiSUM_main Semisumador (.in_1(C), .in_2(main_1_out_3), .out_3(out_4), .out_4(Semisumador_out_4));
  or or_1 (out_5, Semisumador_out_4, main_1_out_4);
endmodule
