// Logisim project Sumador8.circ as structural Verilog: 1 circuit, main circuit Sumador 8 bits
module Sumador_8_bits (
  input  in_1,
  input  [7:0] x,
  input  [7:0] y,
  output [7:0] s,
  output c
);

  wire Sumador_2_out_5, Sumador_3_out_5, Sumador_4_out_5, Sumador_5_out_5, Sumador_6_out_5, Sumador_7_out_5,
       Sumador_out_5;

  Sumador_main Sumador (.C(in_1), .x(x[0]), .y(y[0]), .out_4(s[0]), .out_5(Sumador_out_5));
  Sumador_main Sumador_2 (.C(Sumador_out_5), .x(x[1]), .y(y[1]), .out_4(s[1]), .out_5(Sumador_2_out_5));
  Sumador_main Sumador_3 (.C(Sumador_2_out_5), .x(x[2]), .y(y[2]), .out_4(s[2]), .out_5(Sumador_3_out_5));
  Sumador_main Sumador_4 (.C(Sumador_3_out_5), .x(x[3]), .y(y[3]), .out_4(s[3]), .out_5(Sumador_4_out_5));
  Sumador_main Sumador_5 (.C(Sumador_4_out_5), .x(x[4]), .y(y[4]), .out_4(s[4]), .out_5(Sumador_5_out_5));
  Sumador_main Sumador_6 (.C(Sumador_5_out_5), .x(x[5]), .y(y[5]), .out_4(s[5]), .out_5(Sumador_6_out_5));
  Sumador_main Sumador_7 (.C(Sumador_6_out_5), .x(x[6]), .y(y[6]), .out_4(s[6]), .out_5(Sumador_7_out_5));
  Sumador_main Sumador_8 (.C(Sumador_7_out_5), .x(x[7]), .y(y[7]), .out_4(s[7]), .out_5(c));
endmodule
